// Logisim project lab_01.circ as structural Verilog: 6 circuits, main circuit main
module main (
  input  in_1,
  input  in_2,
  input  in_3,
  input  in_4,
  input  in_5,
  input  in_6,
  input  in_7,
  input  in_8,
  input  in_9,
  output out_10,
  output out_11,
  output out_12,
  output out_13,
  output out_14
);

  fourBitAdder fourbitadder_1 (
    .A4(in_1), .B4(in_2), .A3(in_3), .B3(in_4), .A2(in_5), .B2(in_6), .A1(in_7), .B1(in_8), .C_in(in_9),
    .C_out(out_10), .S4(out_11), .S3(out_12), .S2(out_13), .S1(out_14));
endmodule

module Full_Adder (
  input  A,
  input  B,
  input  C_in,
  output S,
  output C_out
);

  wire and_1_out, and_2_out, xor_1_out;

  xor xor_1 (xor_1_out, A, B);
  xor xor_2 (S, xor_1_out, C_in);
  and and_1 (and_1_out, xor_1_out, C_in);
  and and_2 (and_2_out, A, A);
  or or_1 (C_out, and_1_out, and_2_out);
endmodule

module TwoBitMux (
  input  in_1,
  input  in_2,
  input  in_3,
  output out_4,
  output out_5
);

  wire and_1_out, and_2_out, not_1_out;

  and and_1 (and_1_out, in_1, not_1_out);
  not not_1 (not_1_out, in_3);
  and and_2 (and_2_out, in_2, in_3);
  Multiplexer multiplexer_1 (.in0(in_1), .in1(in_2), .out(out_5), .sel(in_3));
  or or_1 (out_4, and_1_out, and_2_out);
endmodule

module EightBitMux (
  input  in_1,
  input  in_2,
  input  in_3,
  input  in_4,
  input  [1:0] in_5,
  output out_6,
  output out_7
);

  wire multiplexer_1_out, multiplexer_2_out;

  Multiplexer multiplexer_1 (.in0(in_1), .in1(in_2), .out(multiplexer_1_out), .sel(in_5[0]));
  Multiplexer multiplexer_2 (.in0(in_3), .in1(in_4), .out(multiplexer_2_out), .sel(in_5[0]));
  Multiplexer #(.select(2)) multiplexer_3 (.in0(in_1), .in1(in_2), .in2(in_3), .in3(in_4), .out(out_7), .sel(in_5));
  Multiplexer multiplexer_4 (.in0(multiplexer_1_out), .in1(multiplexer_2_out), .out(out_6), .sel(in_5[1]));
endmodule

module fourBitAdder (
  input  A4,
  input  B4,
  input  A3,
  input  B3,
  input  A2,
  input  B2,
  input  A1,
  input  B1,
  input  C_in,
  output C_out,
  output S4,
  output S3,
  output S2,
  output S1
);

  wire full_adder_1_c_out, full_adder_2_c_out, full_adder_3_c_out;

  Full_Adder full_adder_1 (.A(A1), .B(B1), .C_in(C_in), .S(S1), .C_out(full_adder_1_c_out));
  Full_Adder full_adder_2 (.A(A2), .B(B2), .C_in(full_adder_1_c_out), .S(S2), .C_out(full_adder_2_c_out));
  Full_Adder full_adder_3 (.A(A3), .B(B3), .C_in(full_adder_2_c_out), .S(S3), .C_out(full_adder_3_c_out));
  Full_Adder full_adder_4 (.A(A4), .B(B4), .C_in(full_adder_3_c_out), .S(C_out), .C_out(C_out));

  assign S4 = C_out;
endmodule

module twoFullAdders (
  input  in_1,
  input  [1:0] in_2,
  input  [1:0] in_3,
  output S1,
  output S2,
  output S3
);

  wire full_adder_2_c_out;

  Full_Adder full_adder_1 (.A(in_2[1]), .B(in_3[1]), .C_in(full_adder_2_c_out), .S(S1), .C_out(S2));
  Full_Adder full_adder_2 (.A(in_2[0]), .B(in_3[0]), .C_in(in_1), .S(S3), .C_out(full_adder_2_c_out));
endmodule
